// Logisim project NOT-Gate.circ as structural Verilog: 1 circuit, main circuit main
module main (
  input  A,
  output F
);

  not not_1 (F, A);

  // Notes on the sheet:
  //   NOT Gate Circuit
endmodule
