// Logisim project 5-Input-OR-Gate.circ as structural Verilog: 1 circuit, main circuit main
module main (
  input  A,
  input  B,
  input  C,
  input  D,
  input  E,
  output F
);

  wire or_1_out, or_2_out, or_3_out;

  or or_1 (or_1_out, E, D);
  or or_2 (or_2_out, or_1_out, C);
  or or_3 (or_3_out, B, A);
  or or_4 (F, or_2_out, or_3_out);

  // Notes on the sheet:
  //   5-input OR gate circuit
endmodule
