// Logisim project 5-input-AND-Gate.circ as structural Verilog: 1 circuit, main circuit main
module main (
  input  A,
  input  B,
  input  C,
  input  D,
  input  E,
  output X
);

  wire and_1_out, and_2_out, and_3_out;

  and and_1 (and_1_out, A, B);
  and and_2 (and_2_out, and_1_out, C);
  and and_3 (and_3_out, D, E);
  and and_4 (X, and_2_out, and_3_out);

  // Notes on the sheet:
  //   5-input AND gate circuit
endmodule
