// Logisim project 5-input-NAND-Gate.circ as structural Verilog: 1 circuit, main circuit main
module main (
  input  A,
  input  B,
  input  C,
  input  D,
  input  E,
  output F
);

  wire and_1_out, and_2_out, and_3_out;

  and and_1 (and_1_out, A, B);
  and and_2 (and_2_out, and_1_out, C);
  and and_3 (and_3_out, D, E);
  nand nand_1 (F, and_2_out, and_3_out);

  // Notes on the sheet:
  //   5-input NAND gate circuit
endmodule
