// Logisim project 5-input-XNOR-Gate.circ as structural Verilog: 1 circuit, main circuit main
module main (
  input  A,
  input  B,
  input  C,
  input  D,
  input  E,
  output F
);

  wire and_1_out, and_2_out, and_3_out, and_4_out, and_5_out, and_6_out, and_7_out, and_8_out, and_9_out,
       and_10_out, and_11_out, and_12_out, and_13_out, and_14_out, and_15_out, and_16_out, not_1_out,
       not_2_out, not_3_out, not_4_out, not_5_out, not_6_out, not_7_out, not_8_out, not_9_out, not_10_out,
       not_11_out, not_12_out, not_13_out, not_14_out, not_15_out, not_16_out, not_17_out, not_18_out,
       not_19_out, not_20_out, not_21_out, not_22_out, not_23_out, not_24_out, not_25_out, not_26_out,
       not_27_out, not_28_out, not_29_out, not_30_out, not_31_out, not_32_out, not_33_out, not_34_out,
       not_35_out, not_36_out, not_37_out, not_38_out, not_39_out, not_40_out;

  not not_1 (not_1_out, A);
  not not_2 (not_2_out, B);
  not not_3 (not_3_out, C);
  not not_4 (not_4_out, D);
  not not_5 (not_5_out, E);
  not not_6 (not_6_out, C);
  not not_7 (not_7_out, D);
  not not_8 (not_8_out, E);
  not not_9 (not_9_out, B);
  not not_10 (not_10_out, D);
  not not_11 (not_11_out, E);
  not not_12 (not_12_out, B);
  not not_13 (not_13_out, C);
  not not_14 (not_14_out, E);
  not not_15 (not_15_out, B);
  not not_16 (not_16_out, C);
  not not_17 (not_17_out, D);
  not not_18 (not_18_out, A);
  not not_19 (not_19_out, D);
  not not_20 (not_20_out, E);
  not not_21 (not_21_out, A);
  not not_22 (not_22_out, C);
  not not_23 (not_23_out, E);
  not not_24 (not_24_out, A);
  not not_25 (not_25_out, C);
  not not_26 (not_26_out, D);
  not not_27 (not_27_out, A);
  not not_28 (not_28_out, B);
  not not_29 (not_29_out, E);
  not not_30 (not_30_out, A);
  not not_31 (not_31_out, B);
  not not_32 (not_32_out, D);
  not not_33 (not_33_out, A);
  not not_34 (not_34_out, B);
  not not_35 (not_35_out, C);
  not not_36 (not_36_out, E);
  not not_37 (not_37_out, D);
  not not_38 (not_38_out, C);
  not not_39 (not_39_out, B);
  not not_40 (not_40_out, A);
  and and_1 (and_1_out, not_1_out, not_2_out, not_3_out, not_4_out, not_5_out);
  and and_2 (and_2_out, A, B, not_6_out, not_7_out, not_8_out);
  and and_3 (and_3_out, A, not_9_out, C, not_10_out, not_11_out);
  and and_4 (and_4_out, A, not_12_out, not_13_out, D, not_14_out);
  and and_5 (and_5_out, A, not_15_out, not_16_out, not_17_out, E);
  and and_6 (and_6_out, not_18_out, B, C, not_19_out, not_20_out);
  and and_7 (and_7_out, not_21_out, B, not_22_out, D, not_23_out);
  and and_8 (and_8_out, not_24_out, B, not_25_out, not_26_out, E);
  and and_9 (and_9_out, not_27_out, not_28_out, C, D, not_29_out);
  and and_10 (and_10_out, not_30_out, not_31_out, C, not_32_out, E);
  and and_11 (and_11_out, not_33_out, not_34_out, not_35_out, D, E);
  and and_12 (and_12_out, A, B, C, D, not_36_out);
  and and_13 (and_13_out, A, B, C, not_37_out, E);
  and and_14 (and_14_out, A, B, not_38_out, D, E);
  and and_15 (and_15_out, A, not_39_out, C, D, E);
  and and_16 (and_16_out, not_40_out, B, C, D, E);
  or or_1 (F, and_1_out, and_2_out, and_3_out, and_4_out, and_5_out, and_6_out, and_7_out, and_8_out, and_9_out, and_10_out, and_11_out, and_12_out, and_13_out, and_14_out, and_15_out, and_16_out);

  // Notes on the sheet:
  //   5-input XNOR gate circuit
endmodule
