// Logisim project 2-to-1-Line-Multiplexer.circ as structural Verilog: 1 circuit, main circuit main
module main (
  input  S,
  input  I0,
  input  I1,
  output out_4
);

  wire and_1_out, and_2_out, not_1_out;

  not not_1 (not_1_out, S);
  and and_1 (and_1_out, S, I0);
  and and_2 (and_2_out, I1, not_1_out);
  or or_1 (out_4, and_1_out, and_2_out);

  // Notes on the sheet:
  //   2 to 1 Line Multiplexer
endmodule
