// Logisim project 2x1-MUX.circ as structural Verilog: 1 circuit, main circuit main
module main (
  input  I0,
  input  I1,
  input  S0,
  output F
);

  Multiplexer multiplexer_1 (.in0(I0), .in1(I1), .out(F), .sel(S0));  // open: en

  // Notes on the sheet:
  //   2x1 MUX
endmodule
