// Logisim project 4x1-MUX.circ as structural Verilog: 1 circuit, main circuit main
module main (
  input  I0,
  input  I1,
  input  I2,
  input  I3,
  input  [1:0] S1,
  output F
);

  Multiplexer #(.select(2)) multiplexer_1 (.in0(I0), .in1(I1), .in2(I2), .in3(I3), .out(F), .sel(S1));  // open: en

  // Notes on the sheet:
  //   4x1 MUX
  //   S0
endmodule
