// Logisim project 2-to-4-Line-Decoder-with-Enable-Input.circ as structural Verilog: 1 circuit, main circuit main
module main (
  input  E,
  input  A,
  input  B,
  output D0,
  output D1,
  output D2,
  output D3
);

  wire not_1_out, not_2_out, not_3_out, not_4_out;

  or or_1 (D0, B, A, E);
  not not_1 (not_1_out, B);
  not not_2 (not_2_out, A);
  not not_3 (not_3_out, A);
  not not_4 (not_4_out, B);
  or or_2 (D1, not_1_out, A, E);
  or or_3 (D2, not_2_out, B, E);
  or or_4 (D3, not_3_out, not_4_out, E);

  // Notes on the sheet:
  //   2 to 4 Line Decoder with Enable Input
endmodule
