// Logisim project 2-to-4-Line-Decoder.circ as structural Verilog: 1 circuit, main circuit main
module main (
  input  X,
  input  Y,
  output D0,
  output D1,
  output D2,
  output D3
);

  wire not_1_out, not_2_out, not_3_out, not_4_out;

  not not_1 (not_1_out, X);
  not not_2 (not_2_out, Y);
  not not_3 (not_3_out, X);
  not not_4 (not_4_out, Y);
  and and_1 (D3, X, Y);
  and and_2 (D0, not_1_out, not_2_out);
  and and_3 (D1, not_3_out, Y);
  and and_4 (D2, X, not_4_out);

  // Notes on the sheet:
  //   2 to 4 Line Decoder
endmodule
