// Logisim project 3-to-8-Decoder-using-2-to-4-Decoder.circ as structural Verilog: 1 circuit, main circuit main
module main (
  input  X,
  input  [1:0] Y,
  output D0,
  output D1,
  output D2,
  output D3,
  output D4,
  output D5,
  output D6,
  output D7
);

  wire not_1_out;

  not not_1 (not_1_out, X);
  Decoder #(.select(2)) decoder_1 (.out0(D0), .out1(D1), .out2(D2), .out3(D3), .sel(Y), .en(not_1_out));
  Decoder #(.select(2)) decoder_2 (.out0(D4), .out1(D5), .out2(D6), .out3(D7), .sel(Y), .en(X));

  // Notes on the sheet:
  //   X -> MSB
  //   Z -> LSB
  //   Z
  //   3 to 8 Decoder using 2 to 4 Decoder
endmodule
