// Logisim project 3-to-8-Line-Decoder.circ as structural Verilog: 1 circuit, main circuit main
module main (
  input  X,
  input  Y,
  input  Z,
  output D0,
  output D1,
  output D2,
  output D3,
  output D4,
  output D5,
  output D6,
  output D7
);

  wire not_1_out, not_2_out, not_3_out, not_4_out, not_5_out, not_6_out, not_7_out, not_8_out, not_9_out,
       not_10_out, not_11_out, not_12_out;

  not not_1 (not_1_out, X);
  and and_1 (D0, not_1_out, not_2_out, not_3_out);
  not not_2 (not_2_out, Y);
  not not_3 (not_3_out, Z);
  not not_4 (not_4_out, X);
  not not_5 (not_5_out, Y);
  and and_2 (D1, not_4_out, not_5_out, Z);
  not not_6 (not_6_out, X);
  and and_3 (D2, not_6_out, Y, not_7_out);
  not not_7 (not_7_out, Z);
  not not_8 (not_8_out, X);
  and and_4 (D3, not_8_out, Y, Z);
  and and_5 (D4, X, not_9_out, not_10_out);
  not not_9 (not_9_out, Y);
  not not_10 (not_10_out, Z);
  not not_11 (not_11_out, Y);
  and and_6 (D5, X, not_11_out, Z);
  and and_7 (D6, X, Y, not_12_out);
  not not_12 (not_12_out, Z);
  and and_8 (D7, X, Y, Z);

  // Notes on the sheet:
  //   3 to 8 Line Decoder
endmodule
