// Logisim project 4-to-16-Decoder-using-2-to-4-Decoder-and-without-using-Basic-Gates.circ as structural Verilog: 1 circuit, main circuit main
module main (
  input  [1:0] X,
  input  [1:0] Y,
  output D0,
  output D1,
  output D2,
  output D3,
  output D4,
  output D5,
  output D6,
  output D7,
  output D8,
  output D9,
  output D10,
  output D11,
  output D12,
  output D13,
  output D14,
  output D15
);

  wire decoder_1_out0, decoder_1_out1, decoder_1_out2, decoder_1_out3;

  Decoder #(.select(2)) decoder_1 (
    .out0(decoder_1_out0), .out1(decoder_1_out1), .out2(decoder_1_out2), .out3(decoder_1_out3), .sel(X));  // open: en
  Decoder #(.select(2)) decoder_2 (.out0(D0), .out1(D1), .out2(D2), .out3(D3), .sel(Y), .en(decoder_1_out0));
  Decoder #(.select(2)) decoder_3 (.out0(D4), .out1(D5), .out2(D6), .out3(D7), .sel(Y), .en(decoder_1_out1));
  Decoder #(.select(2)) decoder_4 (.out0(D8), .out1(D9), .out2(D10), .out3(D11), .sel(Y), .en(decoder_1_out2));
  Decoder #(.select(2)) decoder_5 (.out0(D12), .out1(D13), .out2(D14), .out3(D15), .sel(Y), .en(decoder_1_out3));

  // Notes on the sheet:
  //   W -> MSB
  //   Z -> LSB
  //   W
  //   Z
  //   4 to 16 Decoder using 2 to 4 Decoder
endmodule
