// Logisim project 4-to-16-Decoder-using-2-to-4-Decoder.circ as structural Verilog: 1 circuit, main circuit main
module main (
  input  W,
  input  X,
  input  [1:0] Z,
  output D0,
  output D1,
  output D2,
  output D3,
  output D4,
  output D5,
  output D6,
  output D7,
  output D8,
  output D9,
  output D10,
  output D11,
  output D12,
  output D13,
  output D14,
  output D15
);

  wire and_1_out, and_2_out, and_3_out, and_4_out, not_1_out, not_2_out, not_3_out, not_4_out;

  not not_1 (not_1_out, W);
  not not_2 (not_2_out, X);
  not not_3 (not_3_out, W);
  not not_4 (not_4_out, X);
  and and_1 (and_1_out, not_1_out, not_2_out);
  and and_2 (and_2_out, not_3_out, X);
  and and_3 (and_3_out, W, not_4_out);
  and and_4 (and_4_out, W, X);
  Decoder #(.select(2)) decoder_1 (.out0(D0), .out1(D1), .out2(D2), .out3(D3), .sel(Z), .en(and_1_out));
  Decoder #(.select(2)) decoder_2 (.out0(D4), .out1(D5), .out2(D6), .out3(D7), .sel(Z), .en(and_2_out));
  Decoder #(.select(2)) decoder_3 (.out0(D8), .out1(D9), .out2(D10), .out3(D11), .sel(Z), .en(and_3_out));
  Decoder #(.select(2)) decoder_4 (.out0(D12), .out1(D13), .out2(D14), .out3(D15), .sel(Z), .en(and_4_out));

  // Notes on the sheet:
  //   W -> MSB
  //   Z -> LSB
  //   Y
  //   4 to 16 Decoder using 2 to 4 Decoder
endmodule
