// Logisim project 4-to-2-Priority-Encoder.circ as structural Verilog: 1 circuit, main circuit main
module main (
  input  D0,
  input  D1,
  input  D2,
  input  D3,
  output [1:0] X
);

  Priority_Encoder #(.select(2)) priority_encoder_1 (
    .in0(D0), .in1(D1), .in2(D2), .in3(D3), .out(X));  // open: gs, en_out, en_in

  // Notes on the sheet:
  //   4 to 2 Priority Encoder
  //   Y
endmodule
