// Logisim project 8-to-3-Priority-Encoder.circ as structural Verilog: 1 circuit, main circuit main
module main (
  input  D0,
  input  D1,
  input  D2,
  input  D3,
  input  D4,
  input  D5,
  input  D6,
  input  D7,
  output [2:0] X
);

  Priority_Encoder priority_encoder_1 (
    .in0(D0), .in1(D1), .in2(D2), .in3(D3), .in4(D4), .in5(D5), .in6(D6), .in7(D7), .out(X));  // open: en_in, gs, en_out

  // Notes on the sheet:
  //   8 to 3 Priority Encoder
  //   Y
  //   Z
endmodule
