// Logisim project 4-bit-Binary-Adder-Subtractor.circ as structural Verilog: 1 circuit, main circuit main
module main (
  input  B3,
  input  A3,
  input  B2,
  input  A2,
  input  B1,
  input  A1,
  input  B0,
  input  A0,
  input  M,
  output Overflow,
  output C4,
  output S3,
  output S2,
  output S1,
  output S0
);

  wire adder_2_cout, adder_3_cout, adder_4_cout, xor_1_out, xor_3_out, xor_4_out, xor_5_out;

  xor xor_1 (xor_1_out, B3, M);
  xor xor_2 (Overflow, C4, adder_2_cout);
  Adder #(.width(1)) adder_1 (.a(xor_1_out), .b(A3), .out(S3), .cin(adder_2_cout), .cout(C4));
  xor xor_3 (xor_3_out, B2, M);
  xor xor_4 (xor_4_out, B1, M);
  Adder #(.width(1)) adder_2 (.a(xor_3_out), .b(A2), .out(S2), .cin(adder_3_cout), .cout(adder_2_cout));
  Adder #(.width(1)) adder_3 (.a(xor_4_out), .b(A1), .out(S1), .cin(adder_4_cout), .cout(adder_3_cout));
  xor xor_5 (xor_5_out, B0, M);
  Adder #(.width(1)) adder_4 (.a(xor_5_out), .b(A0), .out(S0), .cin(M), .cout(adder_4_cout));

  // Notes on the sheet:
  //   Detector
  //   (MSB)
  //   (LSB)
  //   MSB
  //   4 bit Binary Adder Subtractor
  //   LSB
  //   M = 0 (Adder)
  //   M = 1 (Subtractor)
  //   A3 A2 A1 A0
  //   B3 B2 B1 B0
  //   C4 S3 S2 S1 S0
endmodule
