// Logisim project 4-bit-Ripple-Carry-Adder.circ as structural Verilog: 1 circuit, main circuit main
module main (
  input  B3,
  input  A3,
  input  B2,
  input  A2,
  input  B1,
  input  A1,
  input  B0,
  input  A0,
  input  C0,
  output C4,
  output S3,
  output S2,
  output S1,
  output S0
);

  wire adder_2_cout, adder_3_cout, adder_4_cout;

  Adder #(.width(1)) adder_1 (.a(B3), .b(A3), .out(S3), .cin(adder_2_cout), .cout(C4));
  Adder #(.width(1)) adder_2 (.a(B2), .b(A2), .out(S2), .cin(adder_3_cout), .cout(adder_2_cout));
  Adder #(.width(1)) adder_3 (.a(B1), .b(A1), .out(S1), .cin(adder_4_cout), .cout(adder_3_cout));
  Adder #(.width(1)) adder_4 (.a(B0), .b(A0), .out(S0), .cin(C0), .cout(adder_4_cout));

  // Notes on the sheet:
  //   (MSB)
  //   (LSB)
  //   MSB
  //   4 bit Ripple Carry Adder
  //   LSB
  //   A3 A2 A1 A0
  //   B3 B2 B1 B0
  //   C4 S3 S2 S1 S0
endmodule
