// Logisim project Full-Adder.circ as structural Verilog: 1 circuit, main circuit main
module main (
  input  X,
  input  Y,
  input  Z,
  output Carry,
  output Sum
);

  wire and_1_out, and_2_out, and_3_out, and_4_out, and_5_out, and_6_out, and_7_out, and_8_out, and_9_out,
       and_10_out, and_11_out, not_1_out, not_2_out, not_3_out, not_4_out, not_5_out, not_6_out, or_1_out,
       or_3_out, or_4_out;

  and and_1 (and_1_out, Y, Z);
  and and_2 (and_2_out, X, Z);
  not not_1 (not_1_out, X);
  not not_2 (not_2_out, Y);
  not not_3 (not_3_out, X);
  not not_4 (not_4_out, Y);
  or or_1 (or_1_out, and_1_out, and_2_out);
  and and_3 (and_3_out, X, Y);
  and and_4 (and_4_out, not_1_out, not_2_out);
  and and_5 (and_5_out, not_3_out, Y);
  not not_5 (not_5_out, Z);
  and and_6 (and_6_out, X, not_4_out);
  not not_6 (not_6_out, Z);
  and and_7 (and_7_out, X, Y);
  or or_2 (Carry, or_1_out, and_3_out);
  and and_8 (and_8_out, and_4_out, Z);
  and and_9 (and_9_out, and_5_out, not_5_out);
  and and_10 (and_10_out, and_6_out, not_6_out);
  and and_11 (and_11_out, and_7_out, Z);
  or or_3 (or_3_out, and_8_out, and_9_out);
  or or_4 (or_4_out, and_10_out, and_11_out);
  or or_5 (Sum, or_3_out, or_4_out);

  // Notes on the sheet:
  //   Full-Adder
endmodule
