// Logisim project Half-Adder.circ as structural Verilog: 1 circuit, main circuit main
module main (
  input  X,
  input  Y,
  output Carry,
  output Sum
);

  wire and_2_out, and_3_out, not_1_out, not_2_out;

  and and_1 (Carry, X, Y);
  not not_1 (not_1_out, X);
  and and_2 (and_2_out, not_1_out, Y);
  and and_3 (and_3_out, X, not_2_out);
  not not_2 (not_2_out, Y);
  or or_1 (Sum, and_2_out, and_3_out);

  // Notes on the sheet:
  //   Half -Adder
endmodule
