// Logisim project 4-input-function-with-Multiplexer.circ as structural Verilog: 1 circuit, main circuit main
module main (
  input  D,
  input  [2:0] B,
  output F
);

  wire not_1_out;

  not not_1 (not_1_out, D);
  Multiplexer #(.select(3)) multiplexer_1 (
    .in0(D), .in1(D), .in2(not_1_out), .in3(1'b0), .in4(1'b0), .in5(D), .in6(1'b1), .in7(1'b1), .out(F),
    .sel(B));  // open: en

  // Notes on the sheet:
  //   C
  //   A
  //   4 input Function with Multiplexer
  //   F (A,B,C,D) = SOP(1,3,4,11,12,13,14,15)
endmodule
