// Logisim project Boolean-Function-Implementation-using-MUX.circ as structural Verilog: 1 circuit, main circuit main
module main (
  input  Z,
  input  [1:0] X,
  output F
);

  wire not_1_out;

  not not_1 (not_1_out, Z);
  Multiplexer #(.select(2)) multiplexer_1 (
    .in0(Z), .in1(not_1_out), .in2(1'b0), .in3(1'b1), .out(F), .sel(X));  // open: en

  // Notes on the sheet:
  //   Y
  //   Boolean Function Implementation using MUX
  //   F (X,Y,Z) = SOP(1,2,6,7)
endmodule
