// Logisim project Full-Adder-using-4x1-MUX.circ as structural Verilog: 1 circuit, main circuit main
module main (
  input  Z,
  input  [1:0] X,
  output Carry,
  output Sum
);

  wire not_1_out;

  not not_1 (not_1_out, Z);
  Multiplexer #(.select(2)) multiplexer_1 (.in0(1'b0), .in1(Z), .in2(Z), .in3(1'b1), .out(Carry), .sel(X));  // open: en
  Multiplexer #(.select(2)) multiplexer_2 (
    .in0(Z), .in1(not_1_out), .in2(not_1_out), .in3(Z), .out(Sum), .sel(X));  // open: en

  // Notes on the sheet:
  //   Full Adder using 4x1 MUX
  //   Y
  //   X -> MSB
  //   Z -> LSB
endmodule
