// Logisim project Half-Adder-using-2x1-MUX.circ as structural Verilog: 1 circuit, main circuit main
module main (
  input  Y,
  input  X,
  output Carry,
  output Sum
);

  wire not_1_out;

  Multiplexer multiplexer_1 (.in0(1'b0), .in1(Y), .out(Carry), .sel(X));  // open: en
  Multiplexer multiplexer_2 (.in0(Y), .in1(not_1_out), .out(Sum), .sel(X));  // open: en
  not not_1 (not_1_out, Y);

  // Notes on the sheet:
  //   Half Adder using 2x1 MUX
  //   X -> MSB
  //   Y -> LSB
endmodule
