// Logisim project Full-Adder-using-Decoder.circ as structural Verilog: 1 circuit, main circuit main
module main (
  input  [2:0] Z,
  output Carry,
  output Sum
);

  wire decoder_1_out1, decoder_1_out2, decoder_1_out3, decoder_1_out4, decoder_1_out5, decoder_1_out6,
       decoder_1_out7;

  Decoder #(.select(3)) decoder_1 (
    .out1(decoder_1_out1), .out2(decoder_1_out2), .out3(decoder_1_out3), .out4(decoder_1_out4),
    .out5(decoder_1_out5), .out6(decoder_1_out6), .out7(decoder_1_out7), .sel(Z));  // open: out0, en
  or or_1 (Carry, decoder_1_out3, decoder_1_out5, decoder_1_out6, decoder_1_out7);
  or or_2 (Sum, decoder_1_out1, decoder_1_out2, decoder_1_out4, decoder_1_out7);

  // Notes on the sheet:
  //   Y
  //   X
  //   Full Adder using Decoder
  //   C = SOP(3,5,6,7)
  //   S = SOP(1,2,4,7)
endmodule
