// Logisim project SOP-Reduce.circ as structural Verilog: 1 circuit, main circuit main
module main (
  input  A,
  input  B,
  input  C,
  output X
);

  wire and_1_out, and_2_out, not_1_out, not_2_out, not_3_out;

  not not_1 (not_1_out, A);
  not not_2 (not_2_out, C);
  not not_3 (not_3_out, B);
  and and_1 (and_1_out, not_1_out, B, not_2_out);
  and and_2 (and_2_out, A, not_3_out, C);
  or or_1 (X, and_1_out, and_2_out);

  // Notes on the sheet:
  //   F(A,B,C) = SOP(2,5)
endmodule
