// Logisim project SOP.circ as structural Verilog: 1 circuit, main circuit main
module main (
  input  A,
  input  B,
  input  C,
  output F
);

  wire and_1_out, not_1_out, not_2_out;

  not not_1 (not_1_out, A);
  not not_2 (not_2_out, C);
  and and_1 (and_1_out, not_1_out, B);
  or or_1 (F, not_2_out, and_1_out);

  // Notes on the sheet:
  //   F(a,b,c) = SOP(0,2,3,4,6)
endmodule
