// Logisim project Sum of Product.circ as structural Verilog: 2 circuits, main circuit main
module main (
  input  A,
  input  B,
  input  C,
  output X
);

  wire nand_1_out, nand_2_out, nand_3_out, nand_4_out, nand_5_out, nand_6_out, nand_7_out;

  nand nand_1 (nand_1_out, A, A);
  nand nand_2 (nand_2_out, B, B);
  nand nand_3 (nand_3_out, A, A);
  nand nand_4 (nand_4_out, C, C);
  nand nand_5 (nand_5_out, nand_1_out, nand_2_out);
  nand nand_6 (nand_6_out, nand_3_out, nand_4_out);
  nand nand_7 (nand_7_out, A, B, C);
  nand nand_8 (X, nand_5_out, nand_6_out, nand_7_out);
endmodule

module K_Map (
  input  A,
  input  B,
  input  C,
  output X
);

  wire nand_1_out, nand_2_out, nand_3_out, nand_4_out, nand_5_out, nand_6_out, nand_7_out;

  nand nand_1 (nand_1_out, A, A);
  nand nand_2 (nand_2_out, B, B);
  nand nand_3 (nand_3_out, A, A);
  nand nand_4 (nand_4_out, C, C);
  nand nand_5 (nand_5_out, nand_1_out, nand_2_out);
  nand nand_6 (nand_6_out, nand_3_out, nand_4_out);
  nand nand_7 (nand_7_out, A, B, C);
  nand nand_8 (X, nand_5_out, nand_6_out, nand_7_out);
endmodule
