// Logisim project S-R-Flip-Flop-using-D-Flip-Flop.circ as structural Verilog: 1 circuit, main circuit main
module main (
  input  S,
  input  R,
  input  in_3,
  output Q,
  output Q__Inverse
);

  wire and_1_out, clock_1_out, not_1_out, or_1_out;

  Clock clock_1 (.out(clock_1_out));
  not not_1 (not_1_out, R);
  and and_1 (and_1_out, not_1_out, Q);
  or or_1 (or_1_out, S, and_1_out);
  D_Flip_Flop d_ff_1 (.clk(clock_1_out), .D(or_1_out), .Q(Q), .Qn(Q__Inverse), .en(in_3));  // open: preset, reset

  // Notes on the sheet:
  //   CLK
  //   S-R Flip Flop
endmodule
