// Logisim project S-R-Flip-Flop-using-J-K-Flip-Flop.circ as structural Verilog: 1 circuit, main circuit main
module main (
  input  S,
  input  R,
  input  in_3,
  output Q,
  output Q__Inverse
);

  wire clock_1_out;

  Clock clock_1 (.out(clock_1_out));
  J_K_Flip_Flop j_k_ff_1 (.J(S), .clk(clock_1_out), .K(R), .Q(Q), .Qn(Q__Inverse), .en(in_3));  // open: preset, reset

  // Notes on the sheet:
  //   CLK
  //   S-R Flip Flop
endmodule
