// Logisim project S-R-Flip-Flop-using-NOR.circ as structural Verilog: 1 circuit, main circuit main
module main (
  input  S,
  input  R,
  output Q__Inverse,
  output Q
);

  wire and_1_out, and_2_out, clock_1_out;

  Clock clock_1 (.out(clock_1_out));
  and and_1 (and_1_out, S, clock_1_out);
  and and_2 (and_2_out, clock_1_out, R);
  nor nor_1 (Q__Inverse, and_1_out, Q);
  nor nor_2 (Q, Q__Inverse, and_2_out);

  // Notes on the sheet:
  //   CLK
  //   S-R Flip Flop
endmodule
