// Logisim project S-R-Flip-Flop-using-T-Flip-Flop.circ as structural Verilog: 1 circuit, main circuit main
module main (
  input  S,
  input  R,
  input  in_3,
  output Q,
  output Q__Inverse
);

  wire and_1_out, and_2_out, clock_1_out, or_1_out;

  Clock clock_1 (.out(clock_1_out));
  and and_1 (and_1_out, Q__Inverse, S);
  and and_2 (and_2_out, R, Q);
  T_Flip_Flop t_ff_1 (.clk(clock_1_out), .T(or_1_out), .Q(Q), .Qn(Q__Inverse), .en(in_3));  // open: preset, reset
  or or_1 (or_1_out, and_1_out, and_2_out);

  // Notes on the sheet:
  //   CLK
  //   S-R Flip Flop
endmodule
