// Logisim project S-R-Flip-Flop.circ as structural Verilog: 1 circuit, main circuit main
module main (
  input  S,
  input  R,
  input  Enable_PIN,
  output Q,
  output Q__Inverse
);

  wire clock_1_out;

  Clock clock_1 (.out(clock_1_out));
  S_R_Flip_Flop s_r_ff_1 (
    .S(S), .clk(clock_1_out), .R(R), .Q(Q), .Qn(Q__Inverse), .en(Enable_PIN));  // open: preset, reset

  // Notes on the sheet:
  //   CLK
  //   S-R Flip-Flop
endmodule
