// Logisim project J-K-Flip-Flop-using-NAND.circ as structural Verilog: 1 circuit, main circuit main
module main (
  input  J,
  input  K,
  output Q,
  output Q__Inverse
);

  wire clock_1_out, nand_1_out, nand_2_out;

  Clock clock_1 (.out(clock_1_out));
  nand nand_1 (nand_1_out, Q__Inverse, J, clock_1_out);
  nand nand_2 (nand_2_out, clock_1_out, K, Q);
  nand nand_3 (Q, nand_1_out, Q__Inverse);
  nand nand_4 (Q__Inverse, Q, nand_2_out);

  // Notes on the sheet:
  //   CLK
  //   J-K Flip Flop
endmodule
