// Logisim project J-K-Flip-Flop-using-S-R-Flip-Flop.circ as structural Verilog: 1 circuit, main circuit main
module main (
  input  J,
  input  K,
  input  in_3,
  output Q,
  output Q__Inverse
);

  wire and_1_out, and_2_out, clock_1_out;

  Clock clock_1 (.out(clock_1_out));
  and and_1 (and_1_out, Q__Inverse, J);
  and and_2 (and_2_out, K, Q);
  S_R_Flip_Flop s_r_ff_1 (
    .S(and_1_out), .clk(clock_1_out), .R(and_2_out), .Q(Q), .Qn(Q__Inverse), .en(in_3));  // open: preset, reset

  // Notes on the sheet:
  //   J-K Flip Flop
endmodule
