// Logisim project J-K-Flip-Flop.circ as structural Verilog: 1 circuit, main circuit main
module main (
  input  J,
  input  K,
  input  Enable_PIN,
  output Q,
  output Q__Inverse
);

  wire clock_1_out;

  Clock clock_1 (.out(clock_1_out));
  J_K_Flip_Flop j_k_ff_1 (
    .J(J), .clk(clock_1_out), .K(K), .Q(Q), .Qn(Q__Inverse), .en(Enable_PIN));  // open: preset, reset

  // Notes on the sheet:
  //   CLK
  //   J-K Flip-Flop
endmodule
