// Logisim project D-Flip-Flop-using-J-K-Flip-Flop.circ as structural Verilog: 1 circuit, main circuit main
module main (
  input  D,
  input  in_2,
  output Q,
  output Q__Inverse
);

  wire clock_1_out, not_1_out;

  Clock clock_1 (.out(clock_1_out));
  J_K_Flip_Flop j_k_ff_1 (
    .J(D), .clk(clock_1_out), .K(not_1_out), .Q(Q), .Qn(Q__Inverse), .en(in_2));  // open: preset, reset
  not not_1 (not_1_out, D);

  // Notes on the sheet:
  //   CLK
  //   D Flip Flop
endmodule
