// Logisim project D-Flip-Flop-using-NAND.circ as structural Verilog: 1 circuit, main circuit main
module main (
  input  D,
  output Q,
  output Q__Inverse
);

  wire clock_1_out, nand_1_out, nand_2_out, not_1_out;

  Clock clock_1 (.out(clock_1_out));
  not not_1 (not_1_out, D);
  nand nand_1 (nand_1_out, D, clock_1_out);
  nand nand_2 (nand_2_out, clock_1_out, not_1_out);
  nand nand_3 (Q, nand_1_out, Q__Inverse);
  nand nand_4 (Q__Inverse, Q, nand_2_out);

  // Notes on the sheet:
  //   CLK
  //   D Flip Flop
endmodule
