// Logisim project D-Flip-Flop-using-S-R-Flip-Flop.circ as structural Verilog: 1 circuit, main circuit main
module main (
  input  D,
  input  in_2,
  output Q,
  output Q__Inverse
);

  wire clock_1_out, not_1_out;

  Clock clock_1 (.out(clock_1_out));
  not not_1 (not_1_out, D);
  S_R_Flip_Flop s_r_ff_1 (
    .S(D), .clk(clock_1_out), .R(not_1_out), .Q(Q), .Qn(Q__Inverse), .en(in_2));  // open: preset, reset

  // Notes on the sheet:
  //   CLK
  //   D Flip Flop
endmodule
