// Logisim project D-Flip-Flop-using-T-Flip-Flop.circ as structural Verilog: 1 circuit, main circuit main
module main (
  input  D,
  input  in_2,
  output Q,
  output Q__Inverse
);

  wire clock_1_out, xor_1_out;

  Clock clock_1 (.out(clock_1_out));
  xor xor_1 (xor_1_out, Q, D);
  T_Flip_Flop t_ff_1 (.clk(clock_1_out), .T(xor_1_out), .Q(Q), .Qn(Q__Inverse), .en(in_2));  // open: preset, reset

  // Notes on the sheet:
  //   CLK
  //   D Flip Flop
endmodule
