// Logisim project D-Flip-Flop.circ as structural Verilog: 1 circuit, main circuit main
module main (
  input  D,
  input  Enable_PIN,
  output Q,
  output Q__Inverse
);

  wire clock_1_out;

  Clock clock_1 (.out(clock_1_out));
  D_Flip_Flop d_ff_1 (.clk(clock_1_out), .D(D), .Q(Q), .Qn(Q__Inverse), .en(Enable_PIN));  // open: preset, reset

  // Notes on the sheet:
  //   CLK
  //   D Flip-Flop
endmodule
