// Logisim project T-Flip-Flop-using-NAND.circ as structural Verilog: 1 circuit, main circuit main
module main (
  input  T,
  output Q,
  output Q__Inverse
);

  wire clock_1_out, nand_1_out, nand_2_out;

  Clock clock_1 (.out(clock_1_out));
  nand nand_1 (nand_1_out, Q, T, clock_1_out);
  nand nand_2 (nand_2_out, clock_1_out, T, Q__Inverse);
  nand nand_3 (Q, nand_1_out, Q__Inverse);
  nand nand_4 (Q__Inverse, Q, nand_2_out);

  // Notes on the sheet:
  //   CLK
  //   T Flip Flop
endmodule
