// Logisim project T-Flip-Flop-using-NOR.circ as structural Verilog: 1 circuit, main circuit main
module main (
  input  T,
  output Q,
  output Q__Inverse
);

  wire and_1_out, and_2_out, clock_1_out;

  Clock clock_1 (.out(clock_1_out));
  and and_1 (and_1_out, Q, T, clock_1_out);
  and and_2 (and_2_out, clock_1_out, T, Q__Inverse);
  nor nor_1 (Q, and_1_out, Q__Inverse);
  nor nor_2 (Q__Inverse, Q, and_2_out);

  // Notes on the sheet:
  //   CLK
  //   T Flip Flop
endmodule
