// Logisim project T-Flip-Flop-using-S-R-Flip-Flop.circ as structural Verilog: 1 circuit, main circuit main
module main (
  input  T,
  input  in_2,
  output Q,
  output Q__Inverse
);

  wire and_1_out, and_2_out, clock_1_out;

  and and_1 (and_1_out, Q__Inverse, T);
  Clock clock_1 (.out(clock_1_out));
  and and_2 (and_2_out, T, Q);
  S_R_Flip_Flop s_r_ff_1 (
    .S(and_1_out), .clk(clock_1_out), .R(and_2_out), .Q(Q), .Qn(Q__Inverse), .en(in_2));  // open: preset, reset

  // Notes on the sheet:
  //   CLK
  //   T Flip Flop
endmodule
