// Logisim project T-Flip-Flop.circ as structural Verilog: 1 circuit, main circuit main
module main (
  input  T,
  input  Enable_PIN,
  output Q,
  output Q__Inverse
);

  wire clock_1_out;

  Clock clock_1 (.out(clock_1_out));
  T_Flip_Flop t_ff_1 (.clk(clock_1_out), .T(T), .Q(Q), .Qn(Q__Inverse), .en(Enable_PIN));  // open: preset, reset

  // Notes on the sheet:
  //   CLK
  //   T Flip-Flop
endmodule
