// Logisim project 3-bit-Synchronous-Counter-using-various-Flip-Flop.circ as structural Verilog: 1 circuit, main circuit main
module main (
  input  in_1,
  output C,
  output B,
  output A
);

  wire and_1_out, clock_1_out, xor_1_out;

  Clock clock_1 (.out(clock_1_out));
  T_Flip_Flop t_ff_1 (.clk(clock_1_out), .T(in_1), .Q(A), .en(in_1));  // open: Qn, preset, reset
  xor xor_1 (xor_1_out, A, B);
  D_Flip_Flop d_ff_1 (.clk(clock_1_out), .D(xor_1_out), .Q(B), .en(in_1));  // open: Qn, preset, reset
  and and_1 (and_1_out, A, B);
  J_K_Flip_Flop j_k_ff_1 (
    .J(and_1_out), .clk(clock_1_out), .K(and_1_out), .Q(C), .en(in_1));  // open: Qn, preset, reset

  // Notes on the sheet:
  //   LSB
  //   A
  //   B
  //   3-bit Synchronous Counter
  //   MSB
  //   C
endmodule
