// Logisim project 3-bit-Even-Counter.circ as structural Verilog: 1 circuit, main circuit main
module main (
  input  in_1,
  output C,
  output B,
  output A
);

  wire and_1_out, clock_1_out, not_1_out, not_2_out, or_1_out, xor_1_out;

  Clock clock_1 (.out(clock_1_out));
  not not_1 (not_1_out, in_1);
  J_K_Flip_Flop j_k_ff_1 (.J(not_1_out), .clk(clock_1_out), .K(in_1), .Q(A), .en(in_1));  // open: Qn, preset, reset
  or or_1 (or_1_out, B, not_2_out);
  not not_2 (not_2_out, A);
  T_Flip_Flop t_ff_1 (.clk(clock_1_out), .T(or_1_out), .Q(B), .en(in_1));  // open: Qn, preset, reset
  xor xor_1 (xor_1_out, C, B);
  and and_1 (and_1_out, xor_1_out, not_2_out);
  D_Flip_Flop d_ff_1 (.clk(clock_1_out), .D(and_1_out), .Q(C), .en(in_1));  // open: Qn, preset, reset

  // Notes on the sheet:
  //   LSB
  //   A
  //   3 bit Even Counter
  //   B
  //   MSB
  //   C
endmodule
