// Logisim project 3-bit-Odd-Counter.circ as structural Verilog: 1 circuit, main circuit main
module main (
  input  in_1,
  output C,
  output B,
  output A
);

  wire and_1_out, clock_1_out, not_1_out, or_1_out, xor_1_out;

  Clock clock_1 (.out(clock_1_out));
  not not_1 (not_1_out, in_1);
  J_K_Flip_Flop j_k_ff_1 (.J(in_1), .clk(clock_1_out), .K(not_1_out), .Q(A), .en(in_1));  // open: Qn, preset, reset
  or or_1 (or_1_out, B, A);
  T_Flip_Flop t_ff_1 (.clk(clock_1_out), .T(or_1_out), .Q(B), .en(in_1));  // open: Qn, preset, reset
  xor xor_1 (xor_1_out, C, B);
  and and_1 (and_1_out, xor_1_out, A);
  D_Flip_Flop d_ff_1 (.clk(clock_1_out), .D(and_1_out), .Q(C), .en(in_1));  // open: Qn, preset, reset

  // Notes on the sheet:
  //   LSB
  //   A
  //   B
  //   3 bit Odd Counter
  //   MSB
  //   C
endmodule
