// Logisim project MOD-10-Decade-Counter-using-various-Flip-Flop.circ as structural Verilog: 1 circuit, main circuit main
module main (
  input  in_1,
  output D,
  output C,
  output B,
  output A
);

  wire and_1_out, and_2_out, and_3_out, and_4_out, and_5_out, and_6_out, clock_1_out, not_1_out, not_2_out,
       not_3_out, or_1_out, or_2_out, or_3_out, xor_1_out;

  Clock clock_1 (.out(clock_1_out));
  not not_1 (not_1_out, C);
  not not_2 (not_2_out, B);
  or or_1 (or_1_out, and_1_out, not_3_out);
  and and_1 (and_1_out, not_1_out, not_2_out);
  and and_2 (and_2_out, A, not_3_out);
  J_K_Flip_Flop j_k_ff_1 (.J(or_1_out), .clk(clock_1_out), .K(in_1), .Q(A), .en(in_1));  // open: Qn, preset, reset
  and and_3 (and_3_out, D, B);
  or or_2 (or_2_out, and_2_out, and_3_out);
  T_Flip_Flop t_ff_1 (.clk(clock_1_out), .T(or_2_out), .Q(B), .en(in_1));  // open: Qn, preset, reset
  and and_4 (and_4_out, A, B);
  xor xor_1 (xor_1_out, and_4_out, C);
  and and_5 (and_5_out, xor_1_out, not_3_out);
  D_Flip_Flop d_ff_1 (.clk(clock_1_out), .D(and_5_out), .Q(C), .en(in_1));  // open: Qn, preset, reset
  and and_6 (and_6_out, A, B, C);
  or or_3 (or_3_out, B, A, C);
  not not_3 (not_3_out, D);
  J_K_Flip_Flop j_k_ff_2 (.J(and_6_out), .clk(clock_1_out), .K(or_3_out), .Q(D), .en(in_1));  // open: Qn, preset, reset

  // Notes on the sheet:
  //   LSB
  //   A
  //   B
  //   MOD 10 (Decade Counter)
  //   C
  //   MSB
  //   D
endmodule
