// Logisim project MOD-14-Counter.circ as structural Verilog: 1 circuit, main circuit main
module main (
  input  in_1,
  output D,
  output C,
  output B,
  output A
);

  wire and_1_out, and_2_out, and_3_out, clock_1_out;

  Clock clock_1 (.out(clock_1_out));
  J_K_Flip_Flop j_k_ff_1 (
    .J(in_1), .clk(clock_1_out), .K(in_1), .Q(A), .en(in_1), .reset(and_3_out));  // open: Qn, preset
  J_K_Flip_Flop j_k_ff_2 (.J(A), .clk(clock_1_out), .K(A), .Q(B), .en(in_1), .reset(and_3_out));  // open: Qn, preset
  and and_1 (and_1_out, A, B);
  J_K_Flip_Flop j_k_ff_3 (
    .J(and_1_out), .clk(clock_1_out), .K(and_1_out), .Q(C), .en(in_1), .reset(and_3_out));  // open: Qn, preset
  and and_2 (and_2_out, and_1_out, C);
  J_K_Flip_Flop j_k_ff_4 (
    .J(and_2_out), .clk(clock_1_out), .K(and_2_out), .Q(D), .en(in_1), .reset(and_3_out));  // open: Qn, preset
  and and_3 (and_3_out, C, B, D);

  // Notes on the sheet:
  //   CLK
  //   LSB
  //   A
  //   B
  //   MOD 14 Counter
  //   C
  //   MSB
  //   D
endmodule
