// Logisim project MOD-6-Counter.circ as structural Verilog: 1 circuit, main circuit main
module main (
  input  in_1,
  output C,
  output B,
  output A,
  output C_2,
  output B_2,
  output A_2
);

  wire and_1_out, and_2_out, clock_1_out;

  Clock clock_1 (.out(clock_1_out));
  J_K_Flip_Flop j_k_ff_1 (
    .J(in_1), .clk(clock_1_out), .K(in_1), .Q(A), .Qn(A_2), .en(in_1), .reset(and_1_out));  // open: preset
  and and_1 (and_1_out, C, B);
  and and_2 (and_2_out, A, B);
  J_K_Flip_Flop j_k_ff_2 (
    .J(A), .clk(clock_1_out), .K(A), .Q(B), .Qn(B_2), .en(in_1), .reset(and_1_out));  // open: preset
  J_K_Flip_Flop j_k_ff_3 (
    .J(and_2_out), .clk(clock_1_out), .K(and_2_out), .Q(C), .Qn(C_2), .en(in_1), .reset(and_1_out));  // open: preset

  // Notes on the sheet:
  //   LSB
  //   A
  //   B
  //   MOD 6 Counter
  //   MSB
  //   C
endmodule
