// Logisim project MOD-60-Counter.circ as structural Verilog: 1 circuit, main circuit main
module main (
  input  in_1,
  output F,
  output E,
  output D,
  output C,
  output B,
  output A
);

  wire and_1_out, and_2_out, and_3_out, and_4_out, and_5_out, clock_1_out;

  Clock clock_1 (.out(clock_1_out));
  and and_1 (and_1_out, C, D, E, F);
  J_K_Flip_Flop j_k_ff_1 (
    .J(in_1), .clk(clock_1_out), .K(in_1), .Q(A), .en(in_1), .reset(and_1_out));  // open: Qn, preset
  J_K_Flip_Flop j_k_ff_2 (.J(A), .clk(clock_1_out), .K(A), .Q(B), .en(in_1), .reset(and_1_out));  // open: Qn, preset
  and and_2 (and_2_out, A, B);
  and and_3 (and_3_out, and_2_out, C);
  J_K_Flip_Flop j_k_ff_3 (
    .J(and_2_out), .clk(clock_1_out), .K(and_2_out), .Q(C), .en(in_1), .reset(and_1_out));  // open: Qn, preset
  J_K_Flip_Flop j_k_ff_4 (
    .J(and_3_out), .clk(clock_1_out), .K(and_3_out), .Q(D), .en(in_1), .reset(and_1_out));  // open: Qn, preset
  and and_4 (and_4_out, and_3_out, D);
  J_K_Flip_Flop j_k_ff_5 (
    .J(and_4_out), .clk(clock_1_out), .K(and_4_out), .Q(E), .en(in_1), .reset(and_1_out));  // open: Qn, preset
  and and_5 (and_5_out, and_4_out, E);
  J_K_Flip_Flop j_k_ff_6 (
    .J(and_5_out), .clk(clock_1_out), .K(and_5_out), .Q(F), .en(in_1), .reset(and_1_out));  // open: Qn, preset

  // Notes on the sheet:
  //   LSB
  //   A
  //   B
  //   C
  //   D
  //   E
  //   MSB
  //   F
endmodule
