// Logisim project Johnson-Counter.circ as structural Verilog: 1 circuit, main circuit main
module main (
  input  in_1,
  output D,
  output C,
  output B,
  output A
);

  wire clock_1_out;

  Clock clock_1 (.out(clock_1_out));
  D_Flip_Flop d_ff_1 (.clk(clock_1_out), .D(D), .Q(A), .en(in_1));  // open: Qn, preset, reset
  D_Flip_Flop d_ff_2 (.clk(clock_1_out), .D(A), .Q(B), .en(in_1));  // open: Qn, preset, reset
  D_Flip_Flop d_ff_3 (.clk(clock_1_out), .D(B), .Q(C), .en(in_1));  // open: Qn, preset, reset
  D_Flip_Flop d_ff_4 (.clk(clock_1_out), .D(C), .Qn(D), .en(in_1));  // open: Q, preset, reset

  // Notes on the sheet:
  //   CLK
  //   LSB
  //   A
  //   B
  //   Johnson Counter
  //   C
  //   MSB
  //   D
endmodule
