// Logisim project Random-Counter.circ as structural Verilog: 1 circuit, main circuit main
module main (
  input  in_1,
  output C,
  output B,
  output A
);

  wire and_1_out, and_2_out, and_3_out, and_4_out, and_5_out, clock_1_out, not_1_out, not_2_out, not_3_out,
       not_4_out, or_1_out, xnor_1_out;

  Clock clock_1 (.out(clock_1_out));
  not not_1 (not_1_out, C);
  and and_1 (and_1_out, not_1_out, B);
  J_K_Flip_Flop j_k_ff_1 (
    .J(and_1_out), .clk(clock_1_out), .K(xnor_1_out), .Q(A), .en(in_1));  // open: Qn, preset, reset
  xnor xnor_1 (xnor_1_out, C, B);
  and and_2 (and_2_out, B, A);
  or or_1 (or_1_out, and_2_out, and_4_out, and_3_out);
  not not_2 (not_2_out, B);
  not not_3 (not_3_out, C);
  and and_3 (and_3_out, not_2_out, not_3_out);
  and and_4 (and_4_out, B, C);
  T_Flip_Flop t_ff_1 (.clk(clock_1_out), .T(or_1_out), .Q(B), .en(in_1));  // open: Qn, preset, reset
  not not_4 (not_4_out, C);
  and and_5 (and_5_out, A, not_4_out);
  D_Flip_Flop d_ff_1 (.clk(clock_1_out), .D(and_5_out), .Q(C), .en(in_1));  // open: Qn, preset, reset

  // Notes on the sheet:
  //   LSB
  //   A
  //   Random Counter 
  //   B
  //   0 -> 2 -> 3 -> 5 -> 1 -> 6 -> 0
  //   MSB
  //   C
endmodule
