// Logisim project Random-Sequence-Counter.circ as structural Verilog: 1 circuit, main circuit main
module main (
  input  in_1,
  output C,
  output B,
  output A
);

  wire and_1_out, and_2_out, and_3_out, clock_1_out, not_1_out, not_2_out, not_3_out, not_4_out, or_1_out,
       or_2_out, xnor_1_out;

  not not_1 (not_1_out, B);
  not not_2 (not_2_out, A);
  or or_1 (or_1_out, not_2_out, not_1_out, C);
  Clock clock_1 (.out(clock_1_out));
  D_Flip_Flop d_ff_1 (.clk(clock_1_out), .D(or_1_out), .Q(A), .en(in_1));  // open: Qn, preset, reset
  not not_3 (not_3_out, C);
  not not_4 (not_4_out, B);
  and and_1 (and_1_out, A, not_4_out, not_3_out);
  and and_2 (and_2_out, C, C);
  or or_2 (or_2_out, and_1_out, and_2_out);
  T_Flip_Flop t_ff_1 (.clk(clock_1_out), .T(or_2_out), .Q(B), .en(in_1));  // open: Qn, preset, reset
  xnor xnor_1 (xnor_1_out, A, C);
  and and_3 (and_3_out, B, xnor_1_out);
  D_Flip_Flop d_ff_2 (.clk(clock_1_out), .D(and_3_out), .Q(C), .en(in_1));  // open: Qn, preset, reset

  // Notes on the sheet:
  //   CLK
  //   LSB
  //   A
  //   Random Counter ( 1 -> 3 -> 2 -> 7 -> 5 -> 1 )
  //   B
  //   MSB
  //   C
endmodule
