// Logisim project 4-bit-Parallel-in-Parallel-out-Register.circ as structural Verilog: 1 circuit, main circuit main
module main (
  input  D0,
  input  D1,
  input  D2,
  input  D3,
  input  Enable_PIN,
  output Q0,
  output Q1,
  output Q2,
  output Q3
);

  wire clock_1_out;

  Clock clock_1 (.out(clock_1_out));
  D_Flip_Flop d_ff_1 (.clk(clock_1_out), .D(D0), .Q(Q0), .en(Enable_PIN));  // open: Qn, preset, reset
  D_Flip_Flop d_ff_2 (.clk(clock_1_out), .D(D1), .Q(Q1), .en(Enable_PIN));  // open: Qn, preset, reset
  D_Flip_Flop d_ff_3 (.clk(clock_1_out), .D(D2), .Q(Q2), .en(Enable_PIN));  // open: Qn, preset, reset
  D_Flip_Flop d_ff_4 (.clk(clock_1_out), .D(D3), .Q(Q3), .en(Enable_PIN));  // open: Qn, preset, reset

  // Notes on the sheet:
  //   CLK
  //   4 bit Parallel In Parallel Out Register
endmodule
