// Logisim project 4-bit-Parallel-in-Serial-out-Register.circ as structural Verilog: 1 circuit, main circuit main
module main (
  input  in_1,
  input  D1,
  input  D2,
  input  D3,
  input  D0,
  input  Enable_PIN,
  output Q
);

  wire and_1_out, and_2_out, and_3_out, and_4_out, and_5_out, and_6_out, clock_1_out, d_ff_1_q, d_ff_2_q,
       d_ff_3_q, not_1_out, or_1_out, or_2_out, or_3_out;

  Clock clock_1 (.out(clock_1_out));
  not not_1 (not_1_out, in_1);
  D_Flip_Flop d_ff_1 (.clk(clock_1_out), .D(D0), .Q(d_ff_1_q), .en(Enable_PIN));  // open: Qn, preset, reset
  and and_1 (and_1_out, not_1_out, D1);
  and and_2 (and_2_out, d_ff_1_q, in_1);
  or or_1 (or_1_out, and_2_out, and_1_out);
  D_Flip_Flop d_ff_2 (.clk(clock_1_out), .D(or_1_out), .Q(d_ff_2_q), .en(Enable_PIN));  // open: Qn, preset, reset
  and and_3 (and_3_out, d_ff_2_q, in_1);
  and and_4 (and_4_out, not_1_out, D2);
  or or_2 (or_2_out, and_3_out, and_4_out);
  D_Flip_Flop d_ff_3 (.clk(clock_1_out), .D(or_2_out), .Q(d_ff_3_q), .en(Enable_PIN));  // open: Qn, preset, reset
  and and_5 (and_5_out, d_ff_3_q, in_1);
  and and_6 (and_6_out, not_1_out, D3);
  or or_3 (or_3_out, and_5_out, and_6_out);
  D_Flip_Flop d_ff_4 (.clk(clock_1_out), .D(or_3_out), .Q(Q), .en(Enable_PIN));  // open: Qn, preset, reset

  // Notes on the sheet:
  //   Load/Shift Control PIN
  //   0 -> Load Mode
  //   1 -> Shift Mode
  //   CLK
  //   4 bit Parallel in Serial Out Register
endmodule
