// Logisim project 4-bit-Serial-in-Parallel-out-Register.circ as structural Verilog: 1 circuit, main circuit main
module main (
  input  D,
  input  Enable_PIN,
  output Q0,
  output Q1,
  output Q2,
  output Q3
);

  wire clock_1_out;

  Clock clock_1 (.out(clock_1_out));
  D_Flip_Flop d_ff_1 (.clk(clock_1_out), .D(D), .Q(Q0), .en(Enable_PIN));  // open: Qn, preset, reset
  D_Flip_Flop d_ff_2 (.clk(clock_1_out), .D(Q0), .Q(Q1), .en(Enable_PIN));  // open: Qn, preset, reset
  D_Flip_Flop d_ff_3 (.clk(clock_1_out), .D(Q1), .Q(Q2), .en(Enable_PIN));  // open: Qn, preset, reset
  D_Flip_Flop d_ff_4 (.clk(clock_1_out), .D(Q2), .Q(Q3), .en(Enable_PIN));  // open: Qn, preset, reset

  // Notes on the sheet:
  //   CLK
  //   4 bit Serial In Parallel Out Shift Register
endmodule
