// Logisim project 4-bit-Shift-Register.circ as structural Verilog: 1 circuit, main circuit main
module main (
  input  A,
  input  Enable_PIN,
  output F
);

  wire clock_1_out, d_ff_1_q, d_ff_2_q, d_ff_3_q;

  Clock clock_1 (.out(clock_1_out));
  D_Flip_Flop d_ff_1 (.clk(clock_1_out), .D(A), .Q(d_ff_1_q), .en(Enable_PIN));  // open: Qn, preset, reset
  D_Flip_Flop d_ff_2 (.clk(clock_1_out), .D(d_ff_1_q), .Q(d_ff_2_q), .en(Enable_PIN));  // open: Qn, preset, reset
  D_Flip_Flop d_ff_3 (.clk(clock_1_out), .D(d_ff_2_q), .Q(d_ff_3_q), .en(Enable_PIN));  // open: Qn, preset, reset
  D_Flip_Flop d_ff_4 (.clk(clock_1_out), .D(d_ff_3_q), .Q(F), .en(Enable_PIN));  // open: Qn, preset, reset

  // Notes on the sheet:
  //   CLK
  //   4 bit Shift Register (Serial In Serial Out)
endmodule
